# Fritzing sketch Output - soundModuleTwoInput (saved by Fritzing 0.8.5b)
breadboards: 1

parts:
  neopixel1 = Neopixel 24 Ring
  Part2 = Arduino Uno (Rev3)
  C1 = Capacitor [package=cap-pth-small-kit]
  C2 = Capacitor [package=cap-pth-small-kit]
  R3 = Resistor [tolerance=±5% resistance=220 package="0603 [SMD]"]
  R4 = Resistor [tolerance=±5% resistance=220 package="0603 [SMD]"]

nets:
  GND: neopixel1.GND, Part2.GND, C1.2, C2.2
  VCC: neopixel1.Vcc, Part2.5V
  N1: neopixel1.IN, Part2.D6_PWM
  N2: Part2.A0, C1.1, R3.Pin_1
  N3: Part2.A1, C2.1, R4.Pin_1
